// Logisim project 1_bit_equal.circ as structural Verilog: 1 circuit, main circuit main
module main (
  input  in_1,
  input  in_2
);

  wire xnor_1_out;

  xnor xnor_1 (xnor_1_out, in_1, in_2);
  LED led_1 (.in(xnor_1_out));
endmodule
