// Logisim project 4_bit_equal.circ as structural Verilog: 1 circuit, main circuit main
module main (
  input  A,
  input  B
);

  wire and_1_out, and_2_out, xnor_1_out;

  and and_1 (and_1_out, A, ~B);  // AND_Gate
  LED O1 (.in(and_1_out));
  xnor xnor_1 (xnor_1_out, A, B);
  LED O2 (.in(xnor_1_out));
  and and_2 (and_2_out, ~A, B);  // AND_Gate
  LED O3 (.in(and_2_out));
endmodule
