// Logisim project general_comparator_2bit.circ as structural Verilog: 2 circuits, main circuit general_comparator
module general_comparator (
  input  A,
  input  B,
  output O1,
  output O2,
  output O3
);

  and and_1 (O1, A, ~B);  // AND_Gate
  xnor xnor_1 (O2, A, B);
  and and_2 (O3, ~A, B);  // AND_Gate
endmodule

module general2_comparator (
  input  [1:0] A,
  input  [1:0] B
);

  wire and_1_out, and_2_out, and_3_out, general_comparator_1_o1, general_comparator_1_o2,
       general_comparator_1_o3, general_comparator_2_o1, general_comparator_2_o2, general_comparator_2_o3,
       or_1_out, or_2_out;

  general_comparator general_comparator_1 (
    .A(A[1]), .B(B[1]), .O1(general_comparator_1_o1), .O2(general_comparator_1_o2),
    .O3(general_comparator_1_o3));
  general_comparator general_comparator_2 (
    .A(A[0]), .B(B[0]), .O1(general_comparator_2_o1), .O2(general_comparator_2_o2),
    .O3(general_comparator_2_o3));
  and and_1 (and_1_out, general_comparator_1_o2, general_comparator_2_o1);
  and and_2 (and_2_out, general_comparator_1_o2, general_comparator_2_o2);
  and and_3 (and_3_out, general_comparator_1_o2, general_comparator_2_o3);
  or or_1 (or_1_out, general_comparator_1_o1, and_1_out);
  LED led_1 (.in(or_1_out));
  LED led_2 (.in(and_2_out));
  or or_2 (or_2_out, general_comparator_1_o3, and_3_out);
  LED led_3 (.in(or_2_out));
endmodule
