// Logisim project general_comparator_only_nand.circ as structural Verilog: 1 circuit, main circuit main
module main (
  input  A,
  input  B
);

  wire nand_1_out, nand_2_out, nand_3_out, nand_4_out, nand_5_out, nand_6_out, nand_7_out, nand_8_out;

  nand nand_1 (nand_1_out, ~A, ~B);  // NAND_Gate
  nand nand_2 (nand_2_out, nand_1_out, nand_3_out);
  LED O2 (.in(nand_2_out));
  nand nand_3 (nand_3_out, A, B);
  nand nand_4 (nand_4_out, A, ~B);  // NAND_Gate
  nand nand_5 (nand_5_out, nand_4_out, nand_6_out);
  LED O1 (.in(nand_5_out));
  nand nand_6 (nand_6_out, A, ~A);  // NAND_Gate
  nand nand_7 (nand_7_out, ~A, B);  // NAND_Gate
  nand nand_8 (nand_8_out, nand_6_out, nand_7_out);
  LED O3 (.in(nand_8_out));
endmodule
