// Logisim project solutions.circ as structural Verilog
module seg7_test (
  input  [3:0] in_1,
  output out_2,
  output out_3,
  output out_4,
  output out_5,
  output out_6,
  output out_7,
  output out_8
);

  wire m0_out, m1_out, m2_out, m3_out, m4_out, m5_out, m6_out, m7_out, m8_out, m9_out, m10_out, m11_out,
       m12_out, m13_out, m14_out, m15_out;

  and m0 (m0_out, ~in_1[0], ~in_1[1], ~in_1[2], ~in_1[3]);  // AND_Gate
  and m1 (m1_out, in_1[0], ~in_1[1], ~in_1[2], ~in_1[3]);  // AND_Gate
  and m2 (m2_out, ~in_1[0], in_1[1], ~in_1[2], ~in_1[3]);  // AND_Gate
  and m3 (m3_out, in_1[0], in_1[1], ~in_1[2], ~in_1[3]);  // AND_Gate
  and m4 (m4_out, ~in_1[0], ~in_1[1], in_1[2], ~in_1[3]);  // AND_Gate
  and m5 (m5_out, in_1[0], ~in_1[1], in_1[2], ~in_1[3]);  // AND_Gate
  and m6 (m6_out, ~in_1[0], in_1[1], in_1[2], ~in_1[3]);  // AND_Gate
  and m7 (m7_out, in_1[0], in_1[1], in_1[2], ~in_1[3]);  // AND_Gate
  and m8 (m8_out, ~in_1[0], ~in_1[1], ~in_1[2], in_1[3]);  // AND_Gate
  and m9 (m9_out, in_1[0], ~in_1[1], ~in_1[2], in_1[3]);  // AND_Gate
  and m10 (m10_out, ~in_1[0], in_1[1], ~in_1[2], in_1[3]);  // AND_Gate
  and m11 (m11_out, in_1[0], in_1[1], ~in_1[2], in_1[3]);  // AND_Gate
  and m12 (m12_out, ~in_1[0], ~in_1[1], in_1[2], in_1[3]);  // AND_Gate
  and m13 (m13_out, in_1[0], ~in_1[1], in_1[2], in_1[3]);  // AND_Gate
  and m14 (m14_out, ~in_1[0], in_1[1], in_1[2], in_1[3]);  // AND_Gate
  and m15 (m15_out, in_1[0], in_1[1], in_1[2], in_1[3]);
  nor a (out_2, m1_out, m4_out, m11_out, m13_out);
  nor b (out_3, m5_out, m6_out, m11_out, m12_out, m14_out, m15_out);
  nor c (out_4, m2_out, m12_out, m14_out, m15_out);
  nor d (out_5, m1_out, m4_out, m7_out, m10_out, m15_out);
  nor e (out_6, m1_out, m3_out, m4_out, m5_out, m7_out, m9_out);
  nor f (out_7, m1_out, m2_out, m3_out, m7_out, m13_out);
  nor g (out_8, m0_out, m1_out, m7_out, m12_out);
endmodule

module test (
  input  [3:0] in_1
);

  wire seg7_test_1_out_2, seg7_test_1_out_3, seg7_test_1_out_4, seg7_test_1_out_5, seg7_test_1_out_6,
       seg7_test_1_out_7, seg7_test_1_out_8;

  seg7_test seg7_test_1 (
    .in_1(in_1), .out_8(seg7_test_1_out_8), .out_2(seg7_test_1_out_2), .out_3(seg7_test_1_out_3),
    .out_4(seg7_test_1_out_4), .out_5(seg7_test_1_out_5), .out_6(seg7_test_1_out_6), .out_7(seg7_test_1_out_7));
  _7_Segment_Display u_7_segment_display_1 (
    .g(seg7_test_1_out_8), .f(seg7_test_1_out_7), .a(seg7_test_1_out_2), .b(seg7_test_1_out_3),
    .e(seg7_test_1_out_6), .d(seg7_test_1_out_5), .c(seg7_test_1_out_4));  // open: dp
endmodule
