// Logisim project exercise.circ as structural Verilog
module Dim_leds (
);

  wire button_1_out, clock_1_out, nand_1_out;
  wire [1:0] adder_1_out, register_1_q;

  Register #(.width(2)) register_1 (
    .D(adder_1_out), .clk(clock_1_out), .Q(register_1_q), .clr(button_1_out));  // open: en
  Clock clock_1 (.out(clock_1_out));
  Button button_1 (.out(button_1_out));
  Adder #(.width(2)) adder_1 (.a(register_1_q), .b(2'b01), .out(adder_1_out));  // open: cin, cout
  nand nand_1 (nand_1_out, adder_1_out[0], adder_1_out[1]);
  LED led_1 (.in(nand_1_out));
endmodule
