// Logisim project solutions_test.circ as structural Verilog: 4 circuits, main circuit main
module main (
  input  in_1,
  input  in_2,
  input  in_3
);

  wire clock_1_out, output_test_1_l1, output_test_1_l2, output_test_1_l3, output_test_1_r1, output_test_1_r2,
       output_test_1_r3;
  wire [2:0] dflip_flop_3b_1_state_n, state_test_1_out_5;

  state_test state_test_1 (.in_1(dflip_flop_3b_1_state_n), .l(in_1), .r(in_2), .s(in_3), .out_5(state_test_1_out_5));
  Clock clock_1 (.out(clock_1_out));
  Dflip_flop_3b dflip_flop_3b_1 (.state_p(state_test_1_out_5), .clk(clock_1_out), .state_n(dflip_flop_3b_1_state_n));
  output_test output_test_1 (
    .in_1(dflip_flop_3b_1_state_n), .l3(output_test_1_l3), .l2(output_test_1_l2), .l1(output_test_1_l1),
    .r1(output_test_1_r1), .r2(output_test_1_r2), .r3(output_test_1_r3));
  LED led_1 (.in(output_test_1_l3));
  LED led_2 (.in(output_test_1_l2));
  LED led_3 (.in(output_test_1_l1));
  LED led_4 (.in(output_test_1_r1));
  LED led_5 (.in(output_test_1_r2));
  LED led_6 (.in(output_test_1_r3));
endmodule

module state_test (
  input  [2:0] in_1,
  input  l,
  input  r,
  input  s,
  output [2:0] out_5
);

  wire and_1_out, and_2_out, and_3_out, and_5_out, and_6_out, and_7_out, and_9_out, and_10_out, and_11_out,
       and_13_out, and_14_out, and_15_out, and_17_out, and_18_out;

  and and_1 (and_1_out, ~in_1[2], r, ~s);  // AND_Gate
  and and_2 (and_2_out, in_1[2], ~in_1[1], ~s);  // AND_Gate
  or or_1 (out_5[2], and_1_out, and_2_out, and_3_out);
  and and_3 (and_3_out, in_1[2], in_1[1], ~in_1[0], l, ~s);  // AND_Gate
  and and_4 (and_3_out, in_1[2], in_1[1], ~in_1[0], l, ~s);  // AND_Gate
  and and_5 (and_5_out, ~in_1[2], ~in_1[1], ~in_1[0], l, r, ~s);  // AND_Gate
  and and_6 (and_6_out, ~in_1[1], in_1[0], ~s);  // AND_Gate
  and and_7 (and_7_out, ~in_1[2], in_1[1], ~in_1[0], ~s);  // AND_Gate
  and and_8 (and_7_out, ~in_1[2], in_1[1], ~in_1[0], ~s);  // AND_Gate
  and and_9 (and_9_out, ~in_1[2], in_1[1], r, ~s);  // AND_Gate
  or or_2 (out_5[1], and_5_out, and_6_out, and_7_out, and_9_out, and_10_out);
  and and_10 (and_10_out, in_1[2], ~in_1[0], l, ~s);  // AND_Gate
  and and_11 (and_11_out, ~in_1[2], ~in_1[1], ~in_1[0], l, ~s);  // AND_Gate
  and and_12 (and_11_out, ~in_1[2], ~in_1[1], ~in_1[0], l, ~s);  // AND_Gate
  and and_13 (and_13_out, ~in_1[2], in_1[0], r, ~s);  // AND_Gate
  and and_14 (and_14_out, ~in_1[2], in_1[1], ~in_1[0], ~s);  // AND_Gate
  or or_3 (out_5[0], and_11_out, and_13_out, and_14_out, and_15_out, and_17_out, and_18_out);
  and and_15 (and_15_out, in_1[2], ~in_1[1], ~in_1[0], ~s);  // AND_Gate
  and and_16 (and_15_out, in_1[2], ~in_1[1], ~in_1[0], ~s);  // AND_Gate
  and and_17 (and_17_out, in_1[2], ~in_1[1], in_1[0], l, ~s);  // AND_Gate
  and and_18 (and_18_out, in_1[2], in_1[1], ~in_1[0], l, ~s);  // AND_Gate
endmodule

module output_test (
  input  [2:0] in_1,
  output l3,
  output l2,
  output l1,
  output r1,
  output r2,
  output r3
);

  wire and_2_out, and_3_out, and_4_out, and_5_out, and_6_out, and_7_out, and_8_out;

  and and_1 (l3, in_1[1], in_1[0]);
  and and_2 (and_2_out, in_1[1], in_1[0]);
  and and_3 (and_3_out, ~in_1[2], in_1[1], ~in_1[0]);  // AND_Gate
  or or_1 (l2, and_2_out, and_3_out);
  and and_4 (and_4_out, in_1[1], in_1[0]);
  and and_5 (and_5_out, ~in_1[2], in_1[1]);  // AND_Gate
  or or_2 (l1, and_4_out, and_5_out, and_6_out);
  and and_6 (and_6_out, ~in_1[2], ~in_1[1], in_1[0]);  // AND_Gate
  and and_7 (and_7_out, in_1[2], in_1[1]);
  and and_8 (and_8_out, in_1[2], ~in_1[1], in_1[0]);  // AND_Gate
  or or_3 (r2, and_7_out, and_8_out);
  and and_9 (r3, in_1[2], in_1[1]);

  assign r1 = in_1[2];
endmodule

module Dflip_flop_3b (
  input  [2:0] state_p,
  input  clk,
  output [2:0] state_n
);

  D_Flip_Flop d_ff_1 (.D(state_p[2]), .clk(clk), .Q(state_n[2]));  // open: Qn, preset, reset
  D_Flip_Flop d_ff_2 (.D(state_p[1]), .clk(clk), .Q(state_n[1]));  // open: Qn, preset, reset
  D_Flip_Flop d_ff_3 (.D(state_p[0]), .clk(clk), .Q(state_n[0]));  // open: Qn, preset, reset
endmodule
