// Logisim project ALU.circ as structural Verilog
module ALU_OR (
  input  [31:0] A,
  input  [31:0] B,
  output [31:0] C
);

  or or_1 (C[0], A[0], B[0]);
  or or_2 (C[1], A[1], B[1]);
  or or_3 (C[2], A[2], B[2]);
  or or_4 (C[3], A[3], B[3]);
  or or_5 (C[4], A[4], B[4]);
  or or_6 (C[5], A[5], B[5]);
  or or_7 (C[6], A[6], B[6]);
  or or_8 (C[7], A[7], B[7]);
  or or_9 (C[8], A[8], B[8]);
  or or_10 (C[9], A[9], B[9]);
  or or_11 (C[10], A[10], B[10]);
  or or_12 (C[11], A[11], B[11]);
  or or_13 (C[12], A[12], B[12]);
  or or_14 (C[13], A[13], B[13]);
  or or_15 (C[14], A[14], B[14]);
  or or_16 (C[15], A[15], B[15]);
  or or_17 (C[16], A[16], B[16]);
  or or_18 (C[17], A[17], B[17]);
  or or_19 (C[18], A[18], B[18]);
  or or_20 (C[19], A[19], B[19]);
  or or_21 (C[20], A[20], B[20]);
  or or_22 (C[21], A[21], B[21]);
  or or_23 (C[22], A[22], B[22]);
  or or_24 (C[23], A[23], B[23]);
  or or_25 (C[24], A[24], B[24]);
  or or_26 (C[25], A[25], B[25]);
  or or_27 (C[26], A[26], B[26]);
  or or_28 (C[27], A[27], B[27]);
  or or_29 (C[28], A[28], B[28]);
  or or_30 (C[29], A[29], B[29]);
  or or_31 (C[30], A[30], B[30]);
  or or_32 (C[31], A[31], B[31]);
endmodule

module ALU_AND (
  input  [31:0] A,
  input  [31:0] B,
  output [31:0] C
);

  and and_1 (C[0], A[0], B[0]);
  and and_2 (C[1], A[1], B[1]);
  and and_3 (C[2], A[2], B[2]);
  and and_4 (C[3], A[3], B[3]);
  and and_5 (C[4], A[4], B[4]);
  and and_6 (C[5], A[5], B[5]);
  and and_7 (C[6], A[6], B[6]);
  and and_8 (C[7], A[7], B[7]);
  and and_9 (C[8], A[8], B[8]);
  and and_10 (C[9], A[9], B[9]);
  and and_11 (C[10], A[10], B[10]);
  and and_12 (C[11], A[11], B[11]);
  and and_13 (C[12], A[12], B[12]);
  and and_14 (C[13], A[13], B[13]);
  and and_15 (C[14], A[14], B[14]);
  and and_16 (C[15], A[15], B[15]);
  and and_17 (C[16], A[16], B[16]);
  and and_18 (C[17], A[17], B[17]);
  and and_19 (C[18], A[18], B[18]);
  and and_20 (C[19], A[19], B[19]);
  and and_21 (C[20], A[20], B[20]);
  and and_22 (C[21], A[21], B[21]);
  and and_23 (C[22], A[22], B[22]);
  and and_24 (C[23], A[23], B[23]);
  and and_25 (C[24], A[24], B[24]);
  and and_26 (C[25], A[25], B[25]);
  and and_27 (C[26], A[26], B[26]);
  and and_28 (C[27], A[27], B[27]);
  and and_29 (C[28], A[28], B[28]);
  and and_30 (C[29], A[29], B[29]);
  and and_31 (C[30], A[30], B[30]);
  and and_32 (C[31], A[31], B[31]);
endmodule

module ALU_XOR (
  input  [31:0] A,
  input  [31:0] B,
  output [31:0] C
);

  xor xor_1 (C[0], A[0], B[0]);
  xor xor_2 (C[1], A[1], B[1]);
  xor xor_3 (C[2], A[2], B[2]);
  xor xor_4 (C[3], A[3], B[3]);
  xor xor_5 (C[4], A[4], B[4]);
  xor xor_6 (C[5], A[5], B[5]);
  xor xor_7 (C[6], A[6], B[6]);
  xor xor_8 (C[7], A[7], B[7]);
  xor xor_9 (C[8], A[8], B[8]);
  xor xor_10 (C[9], A[9], B[9]);
  xor xor_11 (C[10], A[10], B[10]);
  xor xor_12 (C[11], A[11], B[11]);
  xor xor_13 (C[12], A[12], B[12]);
  xor xor_14 (C[13], A[13], B[13]);
  xor xor_15 (C[14], A[14], B[14]);
  xor xor_16 (C[15], A[15], B[15]);
  xor xor_17 (C[16], A[16], B[16]);
  xor xor_18 (C[17], A[17], B[17]);
  xor xor_19 (C[18], A[18], B[18]);
  xor xor_20 (C[19], A[19], B[19]);
  xor xor_21 (C[20], A[20], B[20]);
  xor xor_22 (C[21], A[21], B[21]);
  xor xor_23 (C[22], A[22], B[22]);
  xor xor_24 (C[23], A[23], B[23]);
  xor xor_25 (C[24], A[24], B[24]);
  xor xor_26 (C[25], A[25], B[25]);
  xor xor_27 (C[26], A[26], B[26]);
  xor xor_28 (C[27], A[27], B[27]);
  xor xor_29 (C[28], A[28], B[28]);
  xor xor_30 (C[29], A[29], B[29]);
  xor xor_31 (C[30], A[30], B[30]);
  xor xor_32 (C[31], A[31], B[31]);
endmodule

module ALU_NOR (
  input  [31:0] A,
  input  [31:0] B,
  output [31:0] C
);

  nor nor_1 (C[0], A[0], B[0]);
  nor nor_2 (C[1], A[1], B[1]);
  nor nor_3 (C[2], A[2], B[2]);
  nor nor_4 (C[3], A[3], B[3]);
  nor nor_5 (C[4], A[4], B[4]);
  nor nor_6 (C[5], A[5], B[5]);
  nor nor_7 (C[6], A[6], B[6]);
  nor nor_8 (C[7], A[7], B[7]);
  nor nor_9 (C[8], A[8], B[8]);
  nor nor_10 (C[9], A[9], B[9]);
  nor nor_11 (C[10], A[10], B[10]);
  nor nor_12 (C[11], A[11], B[11]);
  nor nor_13 (C[12], A[12], B[12]);
  nor nor_14 (C[13], A[13], B[13]);
  nor nor_15 (C[14], A[14], B[14]);
  nor nor_16 (C[15], A[15], B[15]);
  nor nor_17 (C[16], A[16], B[16]);
  nor nor_18 (C[17], A[17], B[17]);
  nor nor_19 (C[18], A[18], B[18]);
  nor nor_20 (C[19], A[19], B[19]);
  nor nor_21 (C[20], A[20], B[20]);
  nor nor_22 (C[21], A[21], B[21]);
  nor nor_23 (C[22], A[22], B[22]);
  nor nor_24 (C[23], A[23], B[23]);
  nor nor_25 (C[24], A[24], B[24]);
  nor nor_26 (C[25], A[25], B[25]);
  nor nor_27 (C[26], A[26], B[26]);
  nor nor_28 (C[27], A[27], B[27]);
  nor nor_29 (C[28], A[28], B[28]);
  nor nor_30 (C[29], A[29], B[29]);
  nor nor_31 (C[30], A[30], B[30]);
  nor nor_32 (C[31], A[31], B[31]);
endmodule

module ArithOut (
  input  [31:0] B,
  input  [31:0] A,
  input  [3:0] Aluop,
  output [31:0] out_4
);

  wire [31:0] addout_1_o;

  AddOut addout_1 (.B(B), .A(A), .sel(Aluop[1]), .O(addout_1_o));
  Multiplexer #(.width(32)) multiplexer_1 (.in0(addout_1_o), .in1({32{addout_1_o[31]}}), .out(out_4), .sel(Aluop[3]));
endmodule

module AddOut (
  input  sel,
  input  [31:0] B,
  input  [31:0] A,
  output [31:0] O
);

  wire [31:0] multiplexer_1_out, not_1_out;

  assign not_1_out = ~B;  // NOT_Gate not_1, 32 bits wide
  Multiplexer #(.width(32)) multiplexer_1 (.in0(B), .in1(not_1_out), .out(multiplexer_1_out), .sel(sel));
  Adder #(.width(32)) adder_1 (.a(multiplexer_1_out), .b(A), .out(O), .cin(sel));  // open: cout
endmodule

module LogicOut (
  input  [3:0] alu_op,
  input  [31:0] A,
  input  [31:0] B,
  output [31:0] O
);

  wire [31:0] alu_and_1_c, alu_nor_1_c, alu_or_1_c, alu_xor_1_c;

  ALU_AND alu_and_1 (.A(A), .B(B), .C(alu_and_1_c));
  ALU_OR alu_or_1 (.A(A), .B(B), .C(alu_or_1_c));
  ALU_XOR alu_xor_1 (.A(A), .B(B), .C(alu_xor_1_c));
  ALU_NOR alu_nor_1 (.A(A), .B(B), .C(alu_nor_1_c));
  Multiplexer #(.select(2), .width(32)) multiplexer_1 (
    .in0(alu_and_1_c), .in1(alu_or_1_c), .in2(alu_xor_1_c), .in3(alu_nor_1_c), .out(O), .sel(alu_op[1:0]));
endmodule

module ALU (
  input  [3:0] Aluop,
  input  [31:0] A,
  input  [31:0] B,
  output [31:0] O
);

  wire [31:0] arithout_1_out_4, logicout_1_o;

  ArithOut arithout_1 (.Aluop(Aluop), .B(B), .A(A), .out_4(arithout_1_out_4));
  LogicOut logicout_1 (.A(A), .B(B), .alu_op(Aluop), .O(logicout_1_o));
  Multiplexer #(.width(32)) multiplexer_1 (.in0(arithout_1_out_4), .in1(logicout_1_o), .out(O), .sel(Aluop[2]));
endmodule
